# Fritzing sketch Monan Live (saved by Fritzing 0.9.9b)

parts:
  MCU1 = Raspberry Pi Zero
  S1 = Taiway 100-SP-X-T1 SPDT Miniature Toggle Switch [part_number=100-SP-X-T1-0-0-B1-M1 package=THT]
  U3 = LIPO-1000mAh [package=lipo-1000]
  M1 = TP4056 Module [part_number=HW-107]
  M2 = MT3608 Module
  Part1 = HC-SR501 Body Sensor Module
  R1 = Resistor [tolerance=±5% power=0.25 resistance=47 package=THT]
  IC1 = Rasberry Pi NIOR Camera [chip_label=IC package="DIP (Dual Inline) [THT]"]  # not connected
  LED1 = smd LED [color="Red (633nm)" package="1206 [SMD]"]

nets:
  N1: MCU1.pin_2, MCU1.pin_4, M2.pin3, Part1.VCC, LED1.anode
  N2: MCU1.pin_6, MCU1.pin_9, MCU1.pin_14, MCU1.pin_30, MCU1.pin_39, M2.pin4, Part1.GND, LED1.cathode
  N3: MCU1.pin_7, R1.Pin_1
  N4: S1.L1, M1.OUT-#4
  N5: S1.L2, M2.pin2
  N6: U3.+, M1.BAT+
  N7: U3.-, M1.BAT-
  N8: M1.OUT-#1, M2.pin1
  N9: Part1.OUT, R1.Pin_0

custom parts:
  TP4056 Module: TP4056 Lithium Battery Charge Management Module Links: TP4056 website
  MT3608 Module: MT3608 Boost Converter Module Links: Aerosemi MT3608 2A Step Up Converter datasheet
  HC-SR501 Body Sensor Module: Pyroelectric Infrared PIR Motion Sensor Detector Module
  Rasberry Pi NIOR Camera: Camera
